// Logisim project CreatingBooleanExpressions.circ as structural Verilog: 1 circuit, main circuit main
module main (
  input  J,
  input  B,
  input  P,
  output D
);

  wire and_1_out, and_2_out, and_3_out;

  and and_1 (and_1_out, J, B);
  and and_2 (and_2_out, B, P);
  and and_3 (and_3_out, P, J);
  or or_1 (D, and_1_out, and_2_out, and_3_out);
endmodule
