// Logisim project MintermsAndMaxterms.circ as structural Verilog: 2 circuits, main circuit SumOfProducts
module SumOfProducts (
  input  in_1,
  input  in_2,
  input  in_3,
  input  in_4,
  output out_5
);

  wire and_1_out, and_2_out;

  and and_1 (and_1_out, ~in_1, in_2, ~in_3, in_4);  // AND_Gate
  and and_2 (and_2_out, in_1, ~in_2, in_3, in_4);  // AND_Gate
  or or_1 (out_5, and_1_out, and_2_out);
endmodule

module ProductOfSums (
  input  A,
  input  B,
  input  C,
  input  D,
  output Y
);

  wire or_1_out, or_2_out;

  or or_1 (or_1_out, ~A, B, ~C, D);  // OR_Gate
  or or_2 (or_2_out, A, ~B, C, D);  // OR_Gate
  and and_1 (Y, or_1_out, or_2_out);
endmodule
