// Logisim project DemorganTheorem.circ as structural Verilog: 3 circuits, main circuit TheoremDefined
module TheoremDefined (
  input  in_1,
  input  in_2,
  output out_3,
  output out_4
);

  nand nand_1 (out_3, in_1, in_2);
  or or_1 (out_4, ~in_1, ~in_2);  // OR_Gate
endmodule

module SimpleExample (
  input  in_1,
  input  in_2,
  input  in_3,
  output out_4,
  output out_5
);

  wire and_1_out, nand_1_out;

  nand nand_1 (nand_1_out, in_2, in_3);
  and and_1 (and_1_out, in_2, ~in_1);  // AND_Gate
  nor nor_1 (out_4, in_1, nand_1_out);
  and and_2 (out_5, and_1_out, in_3);
endmodule

module AboutGrouping (
  input  in_1,
  input  in_2,
  input  in_3,
  input  in_4,
  input  in_5,
  output out_6,
  output out_7
);

  wire and_1_out, nand_1_out, nor_1_out;

  and and_1 (and_1_out, in_2, in_3);
  nand nand_1 (nand_1_out, in_2, ~in_3);  // NAND_Gate
  and and_2 (out_7, in_4, ~in_5);  // AND_Gate
  nor nor_1 (nor_1_out, in_1, and_1_out);
  nor nor_2 (out_6, nor_1_out, nand_1_out);

  // Notes on the sheet:
  //   可以简化为以下电路
endmodule
