// Logisim project multivariateBooleanAlgebra.circ as structural Verilog: 6 circuits, main circuit commutative
module commutative (
  input  A,
  input  B,
  input  in_3,
  input  in_4,
  output Y1,
  output Y2,
  output out_7,
  output out_8
);

  or or_1 (Y1, A, B);
  or or_2 (Y2, B, A);
  and and_1 (out_7, in_3, in_4);
  and and_2 (out_8, in_4, in_3);

  // Notes on the sheet:
  //   Commutative Property for OR
  //   Commutative Property for AND
endmodule

module associative (
  input  A,
  input  B,
  input  C,
  input  in_4,
  input  in_5,
  input  in_6,
  output Y1,
  output Y2,
  output out_9,
  output out_10
);

  wire and_1_out, and_2_out, or_1_out, or_2_out;

  or or_1 (or_1_out, A, B);
  or or_2 (or_2_out, B, C);
  and and_1 (and_1_out, in_4, in_5);
  and and_2 (and_2_out, in_5, in_6);
  or or_3 (Y1, or_1_out, C);
  or or_4 (Y2, A, or_2_out);
  and and_3 (out_9, and_1_out, in_6);
  and and_4 (out_10, in_4, and_2_out);

  // Notes on the sheet:
  //   Association Property for OR
  //   Associative Property for AND
endmodule

module distributiveOrOverAnd (
  input  A,
  input  B,
  input  C,
  output out_4,
  output out_5
);

  wire and_1_out, and_2_out, or_1_out;

  or or_1 (or_1_out, B, C);
  and and_1 (and_1_out, A, B);
  and and_2 (and_2_out, A, C);
  and and_3 (out_4, A, or_1_out);
  or or_2 (out_5, and_1_out, and_2_out);

  // Notes on the sheet:
  //   Distributive Property for OR over AND
endmodule

module distributiveAndOverOr (
  input  A,
  input  B,
  input  C,
  output out_4,
  output out_5
);

  wire and_1_out, or_1_out, or_2_out;

  and and_1 (and_1_out, B, C);
  or or_1 (or_1_out, A, B);
  or or_2 (or_2_out, A, C);
  or or_3 (out_4, A, and_1_out);
  and and_2 (out_5, or_1_out, or_2_out);
endmodule

module absorption (
  input  in_1,
  input  in_2,
  input  in_3,
  input  in_4,
  output out_5,
  output out_6
);

  wire and_1_out, or_1_out;

  and and_1 (and_1_out, in_1, in_2);
  or or_1 (or_1_out, in_3, in_4);
  or or_2 (out_5, in_1, and_1_out);
  and and_2 (out_6, in_3, or_1_out);

  // Notes on the sheet:
  //   Absorption Property Version 1
  //   Absorption Property Version 2
endmodule

module adjacency (
  input  A,
  input  B,
  output out_3
);

  wire and_1_out, and_2_out;

  and and_1 (and_1_out, A, B);
  and and_2 (and_2_out, A, ~B);  // AND_Gate
  or or_1 (out_3, and_1_out, and_2_out);

  // Notes on the sheet:
  //   Adjacency Property
endmodule
