// Logisim project primaryLogicOperations.circ as structural Verilog: 3 circuits, main circuit AndGate
module AndGate (
  input  in_1,
  input  in_2,
  output out_3
);

  and and_1 (out_3, in_1, in_2);

  // Notes on the sheet:
  //   AND Gate
endmodule

module OrGate (
  input  in_1,
  input  in_2,
  output out_3
);

  or or_1 (out_3, in_1, in_2);

  // Notes on the sheet:
  //   OR Gate
endmodule

module NotGate (
  input  in_1,
  output out_2
);

  not not_1 (out_2, in_1);

  // Notes on the sheet:
  //   NOT Gate
endmodule
