// Logisim project secondaryLogicFunctions.circ as structural Verilog: 5 circuits, main circuit NandGate
module NandGate (
  input  in_1,
  input  in_2,
  output out_3
);

  nand nand_1 (out_3, in_1, in_2);

  // Notes on the sheet:
  //   NAND Gate
endmodule

module NorGate (
  input  in_1,
  input  in_2,
  output out_3
);

  nor nor_1 (out_3, in_1, in_2);

  // Notes on the sheet:
  //   NOR Gate
endmodule

module XorGate (
  input  A,
  input  B,
  input  in_3,
  input  in_4,
  output Y,
  output out_6
);

  wire nand_1_out, or_1_out;

  xor xor_1 (Y, A, B);
  nand nand_1 (nand_1_out, in_3, in_4);
  or or_1 (or_1_out, in_4, in_3);
  and and_1 (out_6, nand_1_out, or_1_out);

  // Notes on the sheet:
  //   XOR Gate
  //   XOR Gate Using Three Gate
endmodule

module XnorGate (
  input  in_1,
  input  in_2,
  input  in_3,
  input  in_4,
  output out_5,
  output out_6
);

  wire nand_1_out, or_1_out;

  xnor xnor_1 (out_5, in_1, in_2);
  nand nand_1 (nand_1_out, in_3, in_4);
  or or_1 (or_1_out, in_4, in_3);
  nand nand_2 (out_6, nand_1_out, or_1_out);

  // Notes on the sheet:
  //   XNOR Gate
endmodule

module bufferGate (
  input  in_1,
  output out_2
);

  buf buffer_1 (out_2, in_1);

  // Notes on the sheet:
  //   Buffer Gate
endmodule
