// Logisim project univariateBooleanAlgebra.circ as structural Verilog: 5 circuits, main circuit Identity
module Identity (
  input  in_1,
  input  in_2,
  output out_3,
  output out_4
);

  or or_1 (out_3, in_1, 1'b0);
  and and_1 (out_4, in_2, 1'b1);

  // Notes on the sheet:
  //   OR Identity Element
  //   AND Identity Element
endmodule

module Idempotence (
  input  in_1,
  input  in_2,
  output out_3,
  output out_4
);

  or or_1 (out_3, in_1, in_1);
  and and_1 (out_4, in_2, in_2);

  // Notes on the sheet:
  //   Idempotence for OR Gate
  //   Idempotence for AND Gate
endmodule

module Annihilator (
  input  in_1,
  input  in_2,
  output out_3,
  output out_4
);

  or or_1 (out_3, in_1, 1'b1);
  and and_1 (out_4, in_2, 1'b0);

  // Notes on the sheet:
  //   Annihilator For OR Gate
  //   Annihilator For AND Gate
endmodule

module Complement (
  input  in_1,
  input  A,
  output out_3,
  output Y
);

  or or_1 (out_3, in_1, ~in_1);  // OR_Gate
  and and_1 (Y, A, ~A);  // AND_Gate

  // Notes on the sheet:
  //   OR Complement
  //   A + A' = 1
  //   AND Complement
  //   A * A'  =0
endmodule

module Involution (
  input  in_1,
  output out_2
);

  wire not_1_out;

  not not_1 (not_1_out, in_1);
  not not_2 (out_2, not_1_out);

  // Notes on the sheet:
  //   Involution Property
endmodule
